# Fritzing sketch scheme (saved by Fritzing 0.9.5d)
breadboards: 1

parts:
  Pololu_A1 = Pololu A4988 [package=SO16]
  M1 = Stepper Motor - Bipolar
  MH-ET_LIVE_ESP32_DEVKIT1 = MH-ET LIVE ESP32 DEVKIT 38 pins
  C1 = Electrolytic Capacitor [capacitance=1µF package="100 mil [THT, electrolytic]"]
  J1 = Basic Servo
  J2 = Basic Servo
  VCC1 = 4 x AAA Battery Mount

nets (from the breadboard view):
  GND: Pololu_A1.ENABLE, Pololu_A1.GND, MH-ET_LIVE_ESP32_DEVKIT1.IO34, MH-ET_LIVE_ESP32_DEVKIT1.GND, C1.-, J1.gnd, J2.gnd, VCC1.-
  N1: Pololu_A1.RESET, Pololu_A1.SLEEP
  N2: Pololu_A1.STEP, MH-ET_LIVE_ESP32_DEVKIT1.IO17
  N3: Pololu_A1.DIR, MH-ET_LIVE_ESP32_DEVKIT1.IO16
  VCC: Pololu_A1.VDD, Pololu_A1.VMOT, MH-ET_LIVE_ESP32_DEVKIT1.5V, C1.+, J1.vcc, J2.vcc, VCC1.+
  N4: Pololu_A1.1B, M1.C
  N5: Pololu_A1.1A, M1.A
  N6: Pololu_A1.2A, M1.D
  N7: Pololu_A1.2B, M1.B
  N8: MH-ET_LIVE_ESP32_DEVKIT1.IO18, J1.pulse
  N9: MH-ET_LIVE_ESP32_DEVKIT1.IO5, J2.pulse

custom parts:
  MH-ET LIVE ESP32 DEVKIT 38 pins: http://mh.nodebb.com/topic/2/mh-et-live-esp32-devkit
